// Logisim project FinalProject.circ as structural Verilog: 3 circuits, main circuit ALU_CIRC
module DATAPATH (
  input  [7:0] INP
);

  wire button_1_out, button_2_out, button_3_out, clock_1_out, control_1_ac_write, control_1_alu_source,
       control_1_mem_write, control_1_pc_skip, control_1_pc_source, control_1_pc_write;
  wire [1:0] control_1_ac_source;
  wire [4:0] adder_1_out, control_1_address, multiplexer_1_out, PC_q;
  wire [7:0] AC_q, alu_circ_1_result, INSTRUCTIONS_data, MEMORY_dout, multiplexer_2_out;

  Adder #(.width(5)) adder_1 (.a(5'b00001), .b(PC_q), .out(adder_1_out), .cin(control_1_pc_skip));  // open: cout
  CONTROL control_1 (
    .in_1(INSTRUCTIONS_data), .CURRENT_AC(INSTRUCTIONS_data), .ADDRESS(control_1_address),
    .PC_SOURCE(control_1_pc_source), .PC_SKIP(control_1_pc_skip), .AC_SOURCE(control_1_ac_source),
    .ALU_SOURCE(control_1_alu_source), .MEM_WRITE(control_1_mem_write), .PC_WRITE(control_1_pc_write),
    .AC_WRITE(control_1_ac_write));
  Multiplexer #(.width(5)) multiplexer_1 (
    .in0(control_1_address), .in1(adder_1_out), .out(multiplexer_1_out), .sel(control_1_pc_source));
  Clock clock_1 (.out(clock_1_out));
  Button button_1 (.out(button_1_out));
  Multiplexer #(.select(2), .width(8)) multiplexer_2 (
    .in0(INP), .in1(MEMORY_dout), .in2(alu_circ_1_result), .out(multiplexer_2_out), .sel(control_1_ac_source));  // open: in3
  RAM #(.addrWidth(5), .clearpin("true"), .enables("line")) MEMORY (
    .addr(control_1_address), .we(control_1_mem_write), .clk(clock_1_out), .din(AC_q), .dout(MEMORY_dout),
    .clr(button_2_out));
  ROM #(.addrWidth(5)) INSTRUCTIONS (.addr(PC_q), .data(INSTRUCTIONS_data));
  Register #(.width(5)) PC (
    .D(multiplexer_1_out), .en(control_1_pc_write), .Q(PC_q), .clk(clock_1_out), .clr(button_1_out));
  Button button_2 (.out(button_2_out));
  ALU_CIRC alu_circ_1 (.a(AC_q), .b(MEMORY_dout), .Control(control_1_alu_source), .Result(alu_circ_1_result));
  Button button_3 (.out(button_3_out));
  Register AC (.D(multiplexer_2_out), .en(control_1_ac_write), .Q(AC_q), .clk(clock_1_out), .clr(button_3_out));

  // Notes on the sheet:
  //   contents of INSTRUCTIONS (hex, n*v repeats v):
  //   4c 4f 41 44 9 32 31 a 49 4e 50 55 54 9 30 a 53 54 4f 52 45 9 34 33 a 4c 4f 41 44 9 32 32
endmodule

module ALU_CIRC (
  input  [7:0] a,
  input  [7:0] b,
  input  Control,
  output [7:0] Result
);

  wire [7:0] adder_1_out, subtractor_1_out;

  Adder adder_1 (.a(a), .b(b), .out(adder_1_out));  // open: cin, cout
  Subtractor subtractor_1 (.a(a), .b(b), .out(subtractor_1_out));  // open: bin, bout
  Multiplexer #(.width(8)) multiplexer_1 (.in0(adder_1_out), .in1(subtractor_1_out), .out(Result), .sel(Control));
endmodule

module CONTROL (
  input  [7:0] in_1,
  input  [7:0] CURRENT_AC,
  output [4:0] ADDRESS,
  output PC_SOURCE,
  output PC_SKIP,
  output [1:0] AC_SOURCE,
  output ALU_SOURCE,
  output MEM_WRITE,
  output PC_WRITE,
  output AC_WRITE
);

  wire comparator_1_gt, comparator_1_lt, multiplexer_2_out;
  wire [1:1] multiplexer_1_out;

  Comparator comparator_1 (.a({8{1'b0}}), .b(CURRENT_AC), .gt(comparator_1_gt), .lt(comparator_1_lt));  // open: eq
  Multiplexer #(.select(3), .width(8)) multiplexer_1 (
    .in0(8'hc1), .in1(8'hc5), .in2(8'h61), .in3(8'hc9), .in4(8'hd9), .in5(8'h40), .in6(8'h43),
    .in7({8{1'b0}}),
    .out({AC_WRITE, PC_WRITE, MEM_WRITE, ALU_SOURCE, AC_SOURCE, multiplexer_1_out[1], PC_SOURCE}),
    .sel(in_1[7:5]));
  Multiplexer #(.select(2)) multiplexer_2 (
    .in0(comparator_1_gt), .in2(comparator_1_lt), .out(multiplexer_2_out), .sel(in_1[4:3]));  // open: in1, in3
  and and_1 (PC_SKIP, PC_SOURCE, multiplexer_1_out[1], PC_WRITE, multiplexer_2_out);

  assign ADDRESS = in_1[4:0];
endmodule
